# Fritzing sketch nodemcu 74HC595 (saved by Fritzing 0.9.3b)
breadboards: 1

parts:
  U1 = ESP8266 NodeMCU LoLin module
  U2 = 74HC595 [package="DIP16 [THT]"]
  U3 = 74HC595 [package="DIP16 [THT]"]

nets:
  N1: U1.D0, U1.D1, U2.SH_CP, U2.ST_CP, U3.SH_CP
  N2: U1.D2, U2.DS
  N3: U1.D3, U3.DS
  VCC: U1.3V3, U2.MR, U2.VCC, U3.MR, U3.VCC
  N4: U1.GND, U2.OE, U3.OE

custom parts:
  ESP8266 NodeMCU LoLin module: ESP8266 based NodeMCU
